// Logisim project DesignVorschlag1.2.circ as structural Verilog: 6 circuits, main circuit main
module main (
);

  ALU alu_1 ();  // open: ALU_Function, Operand1, Operand2, ALU_Output, ALU_Flags
endmodule

module ALU (
  input  [3:0] ALU_Function,
  input  [15:0] Operand1,
  input  [15:0] Operand2,
  output [15:0] ALU_Output,
  output [15:0] ALU_Flags
);

  wire and_1_out, and_2_out, arithmeticunit_1_carryout, arithmeticunit_1_overflow, nor_1_out, nor_2_out;
  wire [15:0] arithmeticunit_1_arithmetic_out, logicunit_1_logicalout;

  and and_1 (and_1_out, ~ALU_Function[3], arithmeticunit_1_carryout);  // AND_Gate
  ArithmeticUnit arithmeticunit_1 (
    .ALU_Function(ALU_Function), .Operand1(Operand1), .Operand2(Operand2),
    .Arithmetic_Out(arithmeticunit_1_arithmetic_out), .CarryOut(arithmeticunit_1_carryout),
    .Overflow(arithmeticunit_1_overflow));
  and and_2 (and_2_out, ~ALU_Function[3], arithmeticunit_1_overflow);  // AND_Gate
  LogicUnit logicunit_1 (
    .ALU_Function(ALU_Function), .Operand1(Operand1), .Operand2(Operand2), .LogicalOut(logicunit_1_logicalout));
  Multiplexer #(.width(16)) multiplexer_1 (
    .in0(arithmeticunit_1_arithmetic_out), .in1(logicunit_1_logicalout), .out(ALU_Output),
    .sel(ALU_Function[3]));
  nor nor_1 (nor_1_out, ALU_Output[0], ALU_Output[1], ALU_Output[2], ALU_Output[3], ALU_Output[4], ALU_Output[5], ALU_Output[6], ALU_Output[7], ALU_Output[9], ALU_Output[10], ALU_Output[11], ALU_Output[12], ALU_Output[13], ALU_Output[14], ALU_Output[15], ALU_Output[8]);
  nor nor_2 (nor_2_out, ALU_Output[15], nor_1_out);
  ALUFlagPacker aluflagpacker_1 (
    .CarryFlag(and_1_out), .ZeroFlag(nor_1_out), .SmallerZero(ALU_Output[15]), .BiggerZero(nor_2_out),
    .Overflow(and_2_out), .BoolFlag(ALU_Output[0]), .PackedFlags(ALU_Flags));
endmodule

module LogicUnit (
  input  [3:0] ALU_Function,
  input  [15:0] Operand1,
  input  [15:0] Operand2,
  output [15:0] LogicalOut
);

  wire [15:0] and_1_out, bit_extender_1_out, multiplexer_1_out, or_1_out, xor_1_out;

  assign and_1_out = Operand1 & Operand2;  // AND_Gate and_1, 16 bits wide
  assign or_1_out = Operand1 | Operand2;  // OR_Gate or_1, 16 bits wide
  assign xor_1_out = Operand1 ^ Operand2;  // XOR_Gate xor_1, 16 bits wide
  Multiplexer #(.select(2), .width(16)) multiplexer_1 (
    .in0(Operand1), .in1(and_1_out), .in2(or_1_out), .in3(xor_1_out), .out(multiplexer_1_out),
    .sel(ALU_Function[1:0]));
  assign bit_extender_1_out = {{15{ALU_Function[2]}}, ALU_Function[2]};  // Bit_Extender bit_extender_1
  assign LogicalOut = bit_extender_1_out ^ multiplexer_1_out;  // XOR_Gate xor_2, 16 bits wide

  // Other names for the same wires on the sheet: LogicalFunction[1:0] = ALU_Function[1:0]; Inverted = ALU_Function[2]
endmodule

module ArithmeticUnit (
  input  [3:0] ALU_Function,
  input  [15:0] Operand1,
  input  [15:0] Operand2,
  output [15:0] Arithmetic_Out,
  output CarryOut,
  output Overflow
);

  wire adder_1_cout, subtractor_1_bout, xnor_1_out, xor_1_out, xor_2_out;
  wire [3:0] bit_extender_1_out;
  wire [15:0] adder_1_out, shifter_1_out, shifter_2_out, subtractor_1_out;

  Bit_Extender #(.in_width(16), .out_width(4)) bit_extender_1 (.in(Operand2), .out(bit_extender_1_out));
  Adder #(.width(16)) adder_1 (.a(Operand1), .b(Operand2), .out(adder_1_out), .cout(adder_1_cout));  // open: cin
  Subtractor #(.width(16)) subtractor_1 (
    .a(Operand1), .b(Operand2), .out(subtractor_1_out), .bout(subtractor_1_bout));  // open: bin
  Shifter #(.width(16)) shifter_1 (.in(Operand1), .\dist (bit_extender_1_out), .out(shifter_1_out));
  Shifter #(.shift("lr"), .width(16)) shifter_2 (.in(Operand1), .\dist (bit_extender_1_out), .out(shifter_2_out));
  xor xor_1 (xor_1_out, ALU_Function[0], Operand2[15]);
  xnor xnor_1 (xnor_1_out, xor_1_out, Operand1[15]);
  xor xor_2 (xor_2_out, Operand1[15], Arithmetic_Out[15]);
  Multiplexer #(.select(3), .width(16)) multiplexer_1 (
    .in0(adder_1_out), .in1(subtractor_1_out), .in2(shifter_1_out), .in3(shifter_2_out), .in4({16{1'b0}}),
    .in5({16{1'b0}}), .in6({16{1'b0}}), .in7({16{1'b0}}), .out(Arithmetic_Out), .sel(ALU_Function[2:0]));
  Multiplexer #(.select(3)) multiplexer_2 (
    .in0(adder_1_cout), .in1(subtractor_1_bout), .in2(1'b0), .in3(1'b0), .in4(1'b0), .in5(1'b0), .in6(1'b0),
    .in7(1'b0), .out(CarryOut), .sel(ALU_Function[2:0]));
  and and_1 (Overflow, xnor_1_out, xor_2_out);

  // Other names for the same wires on the sheet: MathFunction[2:0] = ALU_Function[2:0]; S = ALU_Function[0];
  //   Y15 = Arithmetic_Out[15]; A15 = Operand1[15]; B15 = Operand2[15]
endmodule

module ALUFlagPacker (
  input  CarryFlag,
  input  ZeroFlag,
  input  SmallerZero,
  input  BiggerZero,
  input  Overflow,
  input  BoolFlag,
  output [15:0] PackedFlags
);


  assign PackedFlags = {{10{1'b0}}, BoolFlag, Overflow, BiggerZero, SmallerZero, ZeroFlag, CarryFlag};
endmodule

module ALUFlagUnpacker (
  input  [15:0] PackedFlags,
  output CarryFlag,
  output ZeroFlag,
  output SmallerZero,
  output BiggerZero,
  output Overflow,
  output BoolFlag
);


  assign BiggerZero = PackedFlags[3];
  assign BoolFlag = PackedFlags[5];
  assign CarryFlag = PackedFlags[0];
  assign Overflow = PackedFlags[4];
  assign SmallerZero = PackedFlags[2];
  assign ZeroFlag = PackedFlags[1];
endmodule
