// Logisim project DesignVorschlag1.circ as structural Verilog: 6 circuits, main circuit main
module main (
);

  wire button_1_out, CLK, instructiondecoder_1_din_sel, instructiondecoder_1_ram_read,
       instructiondecoder_1_ram_src, instructiondecoder_1_ram_write, instructiondecoder_1_rf_whb,
       instructiondecoder_1_rf_wlb, instructiondecoder_1_use_ma, not_1_out;
  wire [1:0] alu_1_carryflag;
  wire [3:0] alu_1_alu_output, alu_1_alu_output_2, alu_1_alu_output_3, alu_1_alu_output_4,
       bit_extender_1_out, instructiondecoder_1_reg1, instructiondecoder_1_reg2,
       instructiondecoder_1_writereg;
  wire [11:0] instructiondecoder_1_immediate;
  wire [15:0] adder_1_out, bit_extender_2_out, counter_1_q, multiplexer_1_out, multiplexer_2_out,
       multiplexer_3_out, ram_1_dout, regfile_1_ma, regfile_1_operand1, regfile_1_operand2, rom_1_data;

  Clock clock_1 (.out(CLK));
  not not_1 (not_1_out, CLK);
  Button button_1 (.out(button_1_out));
  ROM #(.addrWidth(16), .dataWidth(16)) rom_1 (.addr(counter_1_q), .data(rom_1_data));
  Counter #(.max('hffff), .width(16)) counter_1 (
    .Q(counter_1_q), .clk(not_1_out), .clr(button_1_out));  // open: load, D, count, carry, up
  InstructionDecoder instructiondecoder_1 (
    .Instruction(rom_1_data), .Reg1(instructiondecoder_1_reg1), .Reg2(instructiondecoder_1_reg2),
    .WriteReg(instructiondecoder_1_writereg), .Immediate(instructiondecoder_1_immediate),
    .RF_WLB(instructiondecoder_1_rf_wlb), .RF_WHB(instructiondecoder_1_rf_whb),
    .DIn_Sel(instructiondecoder_1_din_sel), .RAM_Src(instructiondecoder_1_ram_src),
    .RAM_Read(instructiondecoder_1_ram_read), .RAM_Write(instructiondecoder_1_ram_write),
    .USE_MA(instructiondecoder_1_use_ma));
  Multiplexer #(.width(16)) multiplexer_1 (
    .in0(ram_1_dout), .in1(bit_extender_2_out), .out(multiplexer_1_out), .sel(instructiondecoder_1_din_sel));
  Bit_Extender #(.in_width(12), .out_width(4)) bit_extender_1 (
    .in(instructiondecoder_1_immediate), .out(bit_extender_1_out));
  RegFile regfile_1 (
    .WriteData(multiplexer_1_out), .WHB(instructiondecoder_1_rf_whb), .WLB(instructiondecoder_1_rf_wlb),
    .CLK(CLK), .ReadAddress1(instructiondecoder_1_reg1), .ReadAddress2(instructiondecoder_1_reg2),
    .WriteAddress(instructiondecoder_1_writereg),
    .ALU_Output({alu_1_alu_output_4, alu_1_alu_output_3, alu_1_alu_output_2, alu_1_alu_output}),
    .Flags({{14{1'b0}}, alu_1_carryflag}), .Operand1(regfile_1_operand1), .Operand2(regfile_1_operand2),
    .MA(regfile_1_ma));
  assign bit_extender_2_out = {{4{1'b0}}, instructiondecoder_1_immediate};  // Bit_Extender bit_extender_2
  Multiplexer #(.width(16)) multiplexer_2 (
    .in0(regfile_1_operand2), .in1(bit_extender_2_out), .out(multiplexer_2_out),
    .sel(instructiondecoder_1_ram_src));
  Adder #(.width(16)) adder_1 (.a(regfile_1_ma), .b(multiplexer_2_out), .out(adder_1_out));  // open: cin, cout
  Multiplexer #(.width(16)) multiplexer_3 (
    .in0(multiplexer_2_out), .in1(adder_1_out), .out(multiplexer_3_out), .sel(instructiondecoder_1_use_ma));
  Hex_Digit_Display hex_digit_display_1 (.value(alu_1_alu_output_4));  // open: dp
  Hex_Digit_Display hex_digit_display_2 (.value(alu_1_alu_output_3));  // open: dp
  ALU alu_1 (
    .ALU_Function(bit_extender_1_out), .Operand1(regfile_1_operand1), .Operand2(regfile_1_operand2),
    .CarryFlag(alu_1_carryflag[0]),
    .ALU_Output({alu_1_alu_output_4, alu_1_alu_output_3, alu_1_alu_output_2, alu_1_alu_output}),
    .ZeroFlag(alu_1_carryflag[1]));
  Hex_Digit_Display hex_digit_display_3 (.value(alu_1_alu_output_2));  // open: dp
  Hex_Digit_Display hex_digit_display_4 (.value(alu_1_alu_output));  // open: dp
  RAM #(.addrWidth(16), .asyncread("true"), .dataWidth(16)) ram_1 (
    .addr(multiplexer_3_out), .we(instructiondecoder_1_ram_write), .oe(instructiondecoder_1_ram_read),
    .clk(CLK), .dout(ram_1_dout));  // open: din

  // Notes on the sheet:
  //   contents of rom_1 (hex, n*v repeats v):
  //   4001 4102 1001
endmodule

module RegFile (
  input  [15:0] WriteData,
  input  WHB,
  input  WLB,
  input  CLK,
  input  [3:0] ReadAddress1,
  input  [3:0] ReadAddress2,
  input  [3:0] WriteAddress,
  input  [15:0] ALU_Output,
  input  [15:0] Flags,
  output [15:0] Operand1,
  output [15:0] Operand2,
  output [15:0] MA
);

  wire and_1_out, decoder_1_out0, decoder_1_out1, decoder_1_out2, decoder_1_out3, decoder_1_out4,
       decoder_1_out5, decoder_1_out6, decoder_1_out7, decoder_1_out8, decoder_1_out9, decoder_1_out10,
       decoder_1_out11, decoder_1_out12, decoder_1_out13, decoder_1_out14, decoder_1_out15, or_1_out;
  wire [7:0] multiplexer_1_out, multiplexer_2_out, multiplexer_3_out;
  wire [15:0] register_1_q, register_2_q, register_3_q, register_4_q, register_5_q, register_6_q,
       register_7_q, register_8_q, register_9_q, register_10_q, register_12_q, register_13_q, register_14_q,
       register_15_q, register_16_q, WriteRegisterValue;

  Decoder #(.select(4)) decoder_1 (
    .out0(decoder_1_out0), .out1(decoder_1_out1), .out2(decoder_1_out2), .out3(decoder_1_out3),
    .out4(decoder_1_out4), .out5(decoder_1_out5), .out6(decoder_1_out6), .out7(decoder_1_out7),
    .out8(decoder_1_out8), .out9(decoder_1_out9), .out10(decoder_1_out10), .out11(decoder_1_out11),
    .out12(decoder_1_out12), .out13(decoder_1_out13), .out14(decoder_1_out14), .out15(decoder_1_out15),
    .sel(WriteAddress));  // open: en
  Multiplexer #(.width(8)) multiplexer_1 (
    .in0(WriteData[7:0]), .in1(WriteData[15:8]), .out(multiplexer_1_out), .sel(WLB));
  or or_1 (or_1_out, WHB, WLB);
  Multiplexer #(.width(8)) multiplexer_2 (
    .in0(WriteRegisterValue[15:8]), .in1(multiplexer_1_out), .out(multiplexer_2_out), .sel(WHB));
  Multiplexer #(.width(8)) multiplexer_3 (
    .in0(WriteRegisterValue[7:0]), .in1(WriteData[7:0]), .out(multiplexer_3_out), .sel(WLB));
  and and_1 (and_1_out, or_1_out, CLK);
  Register #(.width(16)) register_1 (
    .D({multiplexer_2_out, multiplexer_3_out}), .en(decoder_1_out0), .Q(register_1_q), .clk(and_1_out));  // open: clr
  Register #(.width(16)) register_2 (
    .D({multiplexer_2_out, multiplexer_3_out}), .en(decoder_1_out1), .Q(register_2_q), .clk(and_1_out));  // open: clr
  Register #(.width(16)) register_3 (
    .D({multiplexer_2_out, multiplexer_3_out}), .en(decoder_1_out2), .Q(register_3_q), .clk(and_1_out));  // open: clr
  Register #(.width(16)) register_4 (
    .D({multiplexer_2_out, multiplexer_3_out}), .en(decoder_1_out3), .Q(register_4_q), .clk(and_1_out));  // open: clr
  Register #(.width(16)) register_5 (
    .D({multiplexer_2_out, multiplexer_3_out}), .en(decoder_1_out4), .Q(register_5_q), .clk(and_1_out));  // open: clr
  Register #(.width(16)) register_6 (
    .D({multiplexer_2_out, multiplexer_3_out}), .en(decoder_1_out5), .Q(register_6_q), .clk(and_1_out));  // open: clr
  Register #(.width(16)) register_7 (
    .D({multiplexer_2_out, multiplexer_3_out}), .en(decoder_1_out6), .Q(register_7_q), .clk(and_1_out));  // open: clr
  Register #(.width(16)) register_8 (
    .D({multiplexer_2_out, multiplexer_3_out}), .en(decoder_1_out7), .Q(register_8_q), .clk(and_1_out));  // open: clr
  Register #(.width(16)) register_9 (
    .D({multiplexer_2_out, multiplexer_3_out}), .en(decoder_1_out8), .Q(register_9_q), .clk(and_1_out));  // open: clr
  Register #(.width(16)) register_10 (
    .D({multiplexer_2_out, multiplexer_3_out}), .en(decoder_1_out9), .Q(register_10_q), .clk(and_1_out));  // open: clr
  Register #(.width(16)) register_11 (
    .D({multiplexer_2_out, multiplexer_3_out}), .en(decoder_1_out10), .Q(MA), .clk(and_1_out));  // open: clr
  Register #(.width(16)) register_12 (
    .D({multiplexer_2_out, multiplexer_3_out}), .en(decoder_1_out11), .Q(register_12_q), .clk(and_1_out));  // open: clr
  Register #(.width(16)) register_13 (
    .D({multiplexer_2_out, multiplexer_3_out}), .en(decoder_1_out12), .Q(register_13_q), .clk(and_1_out));  // open: clr
  Register #(.width(16)) register_14 (
    .D({multiplexer_2_out, multiplexer_3_out}), .en(decoder_1_out13), .Q(register_14_q), .clk(and_1_out));  // open: clr
  Register #(.width(16)) register_15 (.D(ALU_Output), .Q(register_15_q), .clk(CLK));  // open: en, clr
  Register #(.width(16)) register_16 (.D(Flags), .Q(register_16_q), .clk(CLK));  // open: en, clr
  Multiplexer #(.select(4), .width(16)) multiplexer_4 (
    .in0(register_1_q), .in1(register_2_q), .in2(register_3_q), .in3(register_4_q), .in4(register_5_q),
    .in5(register_6_q), .in6(register_7_q), .in7(register_8_q), .in8(register_9_q), .in9(register_10_q),
    .in10(MA), .in11(register_12_q), .in12(register_13_q), .in13(register_14_q), .in14(register_15_q),
    .in15(register_16_q), .out(WriteRegisterValue), .sel(WriteAddress));
  Multiplexer #(.select(4), .width(16)) multiplexer_5 (
    .in0(register_1_q), .in1(register_2_q), .in2(register_3_q), .in3(register_4_q), .in4(register_5_q),
    .in5(register_6_q), .in6(register_7_q), .in7(register_8_q), .in8(register_9_q), .in9(register_10_q),
    .in10(MA), .in11(register_12_q), .in12(register_13_q), .in13(register_14_q), .in14(register_15_q),
    .in15(register_16_q), .out(Operand1), .sel(ReadAddress1));
  Multiplexer #(.select(4), .width(16)) multiplexer_6 (
    .in0(register_1_q), .in1(register_2_q), .in2(register_3_q), .in3(register_4_q), .in4(register_5_q),
    .in5(register_6_q), .in6(register_7_q), .in7(register_8_q), .in8(register_9_q), .in9(register_10_q),
    .in10(MA), .in11(register_12_q), .in12(register_13_q), .in13(register_14_q), .in14(register_15_q),
    .in15(register_16_q), .out(Operand2), .sel(ReadAddress2));

  // Other names for the same wires on the sheet: Raw_CLK = CLK
endmodule

module ALU (
  input  [3:0] ALU_Function,
  input  [15:0] Operand1,
  input  [15:0] Operand2,
  output CarryFlag,
  output [15:0] ALU_Output,
  output ZeroFlag
);

  wire arithmeticunit_1_carryout;
  wire [15:0] arithmeticunit_1_arithmetic_out, logicalunit_1_logicalout;

  and and_1 (CarryFlag, ~ALU_Function[3], arithmeticunit_1_carryout);  // AND_Gate
  ArithmeticUnit arithmeticunit_1 (
    .ALU_Function(ALU_Function), .Operand1(Operand1), .Operand2(Operand2),
    .Arithmetic_Out(arithmeticunit_1_arithmetic_out), .CarryOut(arithmeticunit_1_carryout));
  LogicalUnit logicalunit_1 (
    .ALU_Function(ALU_Function), .Operand1(Operand1), .Operand2(Operand2),
    .LogicalOut(logicalunit_1_logicalout));
  Multiplexer #(.width(16)) multiplexer_1 (
    .in0(arithmeticunit_1_arithmetic_out), .in1(logicalunit_1_logicalout), .out(ALU_Output),
    .sel(ALU_Function[3]));
  nor nor_1 (ZeroFlag, ALU_Output[0], ALU_Output[1], ALU_Output[2], ALU_Output[3], ALU_Output[4], ALU_Output[5], ALU_Output[6], ALU_Output[7], ALU_Output[9], ALU_Output[10], ALU_Output[11], ALU_Output[12], ALU_Output[13], ALU_Output[14], ALU_Output[15], ALU_Output[8]);
endmodule

module LogicalUnit (
  input  [3:0] ALU_Function,
  input  [15:0] Operand1,
  input  [15:0] Operand2,
  output [15:0] LogicalOut
);

  wire [15:0] and_1_out, bit_extender_1_out, multiplexer_1_out, or_1_out, xor_1_out;

  assign and_1_out = Operand1 & Operand2;  // AND_Gate and_1, 16 bits wide
  assign or_1_out = Operand1 | Operand2;  // OR_Gate or_1, 16 bits wide
  assign xor_1_out = Operand1 ^ Operand2;  // XOR_Gate xor_1, 16 bits wide
  Multiplexer #(.select(2), .width(16)) multiplexer_1 (
    .in0(Operand1), .in1(and_1_out), .in2(or_1_out), .in3(xor_1_out), .out(multiplexer_1_out),
    .sel(ALU_Function[1:0]));
  assign bit_extender_1_out = {{15{ALU_Function[2]}}, ALU_Function[2]};  // Bit_Extender bit_extender_1
  assign LogicalOut = bit_extender_1_out ^ multiplexer_1_out;  // XOR_Gate xor_2, 16 bits wide

  // Other names for the same wires on the sheet: LogicalFunction[1:0] = ALU_Function[1:0]; Inverted = ALU_Function[2]
endmodule

module ArithmeticUnit (
  input  [3:0] ALU_Function,
  input  [15:0] Operand1,
  input  [15:0] Operand2,
  output [15:0] Arithmetic_Out,
  output CarryOut
);

  wire adder_1_cout, subtractor_1_bout;
  wire [3:0] bit_extender_1_out;
  wire [15:0] adder_1_out, shifter_1_out, shifter_2_out, subtractor_1_out;

  Bit_Extender #(.in_width(16), .out_width(4)) bit_extender_1 (.in(Operand2), .out(bit_extender_1_out));
  Adder #(.width(16)) adder_1 (.a(Operand1), .b(Operand2), .out(adder_1_out), .cout(adder_1_cout));  // open: cin
  Subtractor #(.width(16)) subtractor_1 (
    .a(Operand1), .b(Operand2), .out(subtractor_1_out), .bout(subtractor_1_bout));  // open: bin
  Shifter #(.width(16)) shifter_1 (.in(Operand1), .\dist (bit_extender_1_out), .out(shifter_1_out));
  Shifter #(.shift("lr"), .width(16)) shifter_2 (.in(Operand1), .\dist (bit_extender_1_out), .out(shifter_2_out));
  Multiplexer #(.select(3), .width(16)) multiplexer_1 (
    .in0(adder_1_out), .in1(subtractor_1_out), .in2(shifter_1_out), .in3(shifter_2_out), .in4({16{1'b0}}),
    .in5({16{1'b0}}), .in6({16{1'b0}}), .in7({16{1'b0}}), .out(Arithmetic_Out), .sel(ALU_Function[2:0]));
  Multiplexer #(.select(3)) multiplexer_2 (
    .in0(adder_1_cout), .in1(subtractor_1_bout), .in2(1'b0), .in3(1'b0), .in4(1'b0), .in5(1'b0), .in6(1'b0),
    .in7(1'b0), .out(CarryOut), .sel(ALU_Function[2:0]));

  // Other names for the same wires on the sheet: MathFunction[2:0] = ALU_Function[2:0]
endmodule

module InstructionDecoder (
  input  [15:0] Instruction,
  output [3:0] Reg1,
  output [3:0] Reg2,
  output [3:0] WriteReg,
  output [11:0] Immediate,
  output RF_WLB,
  output RF_WHB,
  output DIn_Sel,
  output RAM_Src,
  output RAM_Read,
  output RAM_Write,
  output USE_MA
);

  wire comparator_1_eq, comparator_2_eq, comparator_3_eq, comparator_4_eq, comparator_5_eq, comparator_6_eq;
  wire [11:0] bit_extender_1_out, bit_extender_2_out, bit_extender_3_out, bit_extender_4_out;

  Comparator #(.mode("unsigned"), .width(4)) comparator_1 (
    .a(Instruction[15:12]), .b(4'b0100), .eq(comparator_1_eq));  // open: gt, lt
  Comparator #(.mode("unsigned"), .width(4)) comparator_2 (
    .a(Instruction[15:12]), .b(4'b0101), .eq(comparator_2_eq));  // open: gt, lt
  Comparator #(.mode("unsigned"), .width(4)) comparator_3 (
    .a(Instruction[15:12]), .b(4'b0010), .eq(comparator_3_eq));  // open: gt, lt
  Comparator #(.mode("unsigned"), .width(4)) comparator_4 (
    .a(Instruction[15:12]), .b(4'b0110), .eq(comparator_4_eq));  // open: gt, lt
  Comparator #(.mode("unsigned"), .width(4)) comparator_5 (
    .a(Instruction[15:12]), .b(4'b0011), .eq(comparator_5_eq));  // open: gt, lt
  Comparator #(.mode("unsigned"), .width(4)) comparator_6 (
    .a(Instruction[15:12]), .b(4'b0111), .eq(comparator_6_eq));  // open: gt, lt
  or or_1 (RF_WLB, comparator_1_eq, comparator_3_eq, comparator_4_eq);
  or or_2 (RF_WHB, comparator_2_eq, comparator_3_eq, comparator_4_eq);
  or or_3 (DIn_Sel, comparator_2_eq, comparator_1_eq);
  or or_4 (RAM_Read, comparator_4_eq, comparator_3_eq);
  or or_5 (RAM_Src, comparator_3_eq, comparator_5_eq);
  or or_6 (RAM_Write, comparator_5_eq, comparator_6_eq);
  assign bit_extender_1_out = {{8{1'b0}}, Instruction[11:8]};  // Bit_Extender bit_extender_1
  assign bit_extender_2_out = {{4{1'b0}}, Instruction[7:0]};  // Bit_Extender bit_extender_2
  assign bit_extender_3_out = {{4{1'b0}}, Instruction[7:0]};  // Bit_Extender bit_extender_3
  assign bit_extender_4_out = {{8{1'b0}}, Instruction[11:8]};  // Bit_Extender bit_extender_4
  Multiplexer #(.select(4), .width(4)) multiplexer_1 (
    .in1(Instruction[7:4]), .in3(Instruction[11:8]), .in7(Instruction[11:8]), .in14(Instruction[3:0]),
    .in15(Instruction[7:4]), .out(Reg1), .sel(Instruction[15:12]));  // open: in0, in2, in4, in5, in6, in8, in9, in10, in11, in12, in13
  Multiplexer #(.select(4), .width(4)) multiplexer_2 (
    .in1(Instruction[3:0]), .in6(Instruction[7:4]), .in7(Instruction[7:4]), .in15(Instruction[3:0]),
    .out(Reg2), .sel(Instruction[15:12]));  // open: in0, in2, in3, in4, in5, in8, in9, in10, in11, in12, in13, in14
  Multiplexer #(.select(4), .width(4)) multiplexer_3 (
    .in2(Instruction[11:8]), .in4(Instruction[11:8]), .in5(Instruction[11:8]), .in6(Instruction[11:8]),
    .in14(Instruction[11:8]), .out(WriteReg), .sel(Instruction[15:12]));  // open: in0, in1, in3, in7, in8, in9, in10, in11, in12, in13, in15
  Multiplexer #(.select(4), .width(12)) multiplexer_4 (
    .in1(bit_extender_1_out), .in2(bit_extender_2_out), .in3(bit_extender_2_out), .in4(bit_extender_3_out),
    .in5(bit_extender_3_out), .in8(Instruction[11:0]), .in9(Instruction[11:0]), .in10(Instruction[11:0]),
    .in11(Instruction[11:0]), .in12(Instruction[11:0]), .in13(Instruction[11:0]), .in15(bit_extender_4_out),
    .out(Immediate), .sel(Instruction[15:12]));  // open: in0, in6, in7, in14

  assign USE_MA = Instruction[0];

  // Other names for the same wires on the sheet: RawInstr[15:0] = Instruction;
  //   InstructionName[3:0] = Instruction[15:12]
endmodule
